# Fritzing sketch prototype_wiring (saved by Fritzing 1.0.8)
breadboards: 1

parts:
  Mod1 = Raspberry Pi 4B
  Part1 = Adafruit SCD4x [part_number="Adafruit #5187"]
  SG1 = Buzzer 12mm [package=buzzer-ccv-kit]
  R2 = Resistor [tolerance=±5% resistance=220 package="0603 [SMD]"]
  LED1 = LEDs [package=led10mm]
  R3 = Resistor [tolerance=±5% resistance=220 package="0603 [SMD]"]
  R4 = Resistor [tolerance=±5% resistance=220 package="0603 [SMD]"]

nets:
  3V3: Mod1.3V3, Part1.VCC
  N1: Mod1.GPIO2, Part1.SDA
  N2: Mod1.GPIO3, Part1.SCL
  GND: Mod1.GND, Part1.GND, SG1.1, LED1.A
  N3: Mod1.GPIO17, R4.Pin_1
  N4: Mod1.GPIO18, R2.Pin_1
  N5: SG1.2, R3.Pin_0
  N6: R2.Pin_0, LED1.C
  N7: R3.Pin_1, R4.Pin_0

custom parts:
  Adafruit SCD4x: Take a deep breath in...now slowly breathe out. Mmm isn't it wonderful? All that air around us, which we bring into our lungs, extracts oxygen from and then breathes out carbon dioxide. CO2 is essential for life on this planet we call Earth - we and plants take turns using and emitting CO2 in an elegant symbiosis. But it's important to keep that CO2 balanced - you don't want too much around,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
